// Logisim project DecoOpALU.circ as structural Verilog: 9 circuits, main circuit Principal
module Principal (
);

  wire funcion_1_add, funcion_1_and, funcion_1_or, funcion_1_slt, funcion_1_sub, opalu_2_out;
  wire [3:0] controladordisp_1_out_2, controladordisp_1_out_3, controladordisp_2_out_2,
       controladordisp_2_out_3, controladordisp_3_out_2, controladordisp_3_out_3;
  wire [31:0] instruction_memory_1_instruction;

  Instruction_memory instruction_memory_1 (.Read_address(32'h8), .Instruction(instruction_memory_1_instruction));
  LED OPALU (.in(opalu_2_out));
  OpALU opalu_2 (.in_1(instruction_memory_1_instruction[31:26]), .OUT(opalu_2_out));
  Hex_Digit_Display hex_digit_display_1 (.value(controladordisp_1_out_3));  // open: dp
  ControladorDisp controladordisp_1 (
    .in_1(instruction_memory_1_instruction[25:21]), .out_2(controladordisp_1_out_2),
    .out_3(controladordisp_1_out_3));
  Hex_Digit_Display hex_digit_display_2 (.value(controladordisp_2_out_3));  // open: dp
  ControladorDisp controladordisp_2 (
    .in_1(instruction_memory_1_instruction[20:16]), .out_2(controladordisp_2_out_2),
    .out_3(controladordisp_2_out_3));
  Hex_Digit_Display hex_digit_display_3 (.value(controladordisp_3_out_3));  // open: dp
  ControladorDisp controladordisp_3 (
    .in_1(instruction_memory_1_instruction[15:11]), .out_2(controladordisp_3_out_2),
    .out_3(controladordisp_3_out_3));
  LED ADD (.in(funcion_1_add));
  funcion funcion_1 (
    .funcion(instruction_memory_1_instruction[5:0]), .ADD(funcion_1_add), .SUB(funcion_1_sub),
    .AND(funcion_1_and), .OR(funcion_1_or), .SLT(funcion_1_slt));
  LED SUB (.in(funcion_1_sub));
  LED AND (.in(funcion_1_and));
  LED OR (.in(funcion_1_or));
  LED SLT (.in(funcion_1_slt));
  Hex_Digit_Display hex_digit_display_4 (.value(controladordisp_1_out_2));  // open: dp
  Hex_Digit_Display hex_digit_display_5 (.value(controladordisp_2_out_2));  // open: dp
  Hex_Digit_Display hex_digit_display_6 (.value(controladordisp_3_out_2));  // open: dp

  // Notes on the sheet:
  //   OPCODE
  //   instruccion[31:26]
  //   RS
  //   instruccion[25:21]
  //   RT
  //   instruccion[20:16]
  //   RD
  //   instruccion[15:11]
  //   FUNCION
  //   instruccion[5:0]
endmodule

module Register_file (
  input  clk,
  input  reset,
  input  [4:0] Read_Register_1,
  input  [4:0] Read_Register_2,
  input  [4:0] Write_Register,
  input  [31:0] Write_Data,
  input  Write,
  output [31:0] Read_Data_1,
  output [31:0] Read_Data_2
);

  wire decoder_1_out1, decoder_1_out2, decoder_1_out3, decoder_1_out4, decoder_1_out5, decoder_1_out6,
       decoder_1_out7, decoder_1_out8, decoder_1_out9, decoder_1_out10, decoder_1_out11, decoder_1_out12,
       decoder_1_out13, decoder_1_out14, decoder_1_out15, decoder_1_out16, decoder_1_out17, decoder_1_out18,
       decoder_1_out19, decoder_1_out20, decoder_1_out21, decoder_1_out22, decoder_1_out23, decoder_1_out24,
       decoder_1_out25, decoder_1_out26, decoder_1_out27, decoder_1_out28, decoder_1_out29, decoder_1_out30,
       decoder_1_out31;
  wire [31:0] delayer1x32_1_p2, multiplexer_1_out, multiplexer_2_out, R1_q, R2_q, R3_q, R4_q, R5_q, R6_q,
       R7_q, R8_q, R9_q, R10_q, R11_q, R12_q, R13_q, R14_q, R15_q, R16_q, R17_q, R18_q, R19_q, R20_q, R21_q,
       R22_q, R23_q, R24_q, R25_q, R26_q, R27_q, R28_q, R29_q, R30_q, R31_q;

  Decoder #(.select(5), .disabled(0)) decoder_1 (
    .out1(decoder_1_out1), .out2(decoder_1_out2), .out3(decoder_1_out3), .out4(decoder_1_out4),
    .out5(decoder_1_out5), .out6(decoder_1_out6), .out7(decoder_1_out7), .out8(decoder_1_out8),
    .out9(decoder_1_out9), .out10(decoder_1_out10), .out11(decoder_1_out11), .out12(decoder_1_out12),
    .out13(decoder_1_out13), .out14(decoder_1_out14), .out15(decoder_1_out15), .out16(decoder_1_out16),
    .out17(decoder_1_out17), .out18(decoder_1_out18), .out19(decoder_1_out19), .out20(decoder_1_out20),
    .out21(decoder_1_out21), .out22(decoder_1_out22), .out23(decoder_1_out23), .out24(decoder_1_out24),
    .out25(decoder_1_out25), .out26(decoder_1_out26), .out27(decoder_1_out27), .out28(decoder_1_out28),
    .out29(decoder_1_out29), .out30(decoder_1_out30), .out31(decoder_1_out31), .sel(Write_Register),
    .en(Write));  // open: out0
  // Delayer1x32 delayer1x32_1: pin names not known; wires that end beside it: Write_Data, delayer1x32_1_p2
  Register #(.width(32)) R1 (.D(delayer1x32_1_p2), .en(decoder_1_out1), .Q(R1_q), .clk(clk), .clr(reset));
  Register #(.width(32)) R2 (.D(delayer1x32_1_p2), .en(decoder_1_out2), .Q(R2_q), .clk(clk), .clr(reset));
  Register #(.width(32)) R3 (.D(delayer1x32_1_p2), .en(decoder_1_out3), .Q(R3_q), .clk(clk), .clr(reset));
  Register #(.width(32)) R4 (.D(delayer1x32_1_p2), .en(decoder_1_out4), .Q(R4_q), .clk(clk), .clr(reset));
  Register #(.width(32)) R5 (.D(delayer1x32_1_p2), .en(decoder_1_out5), .Q(R5_q), .clk(clk), .clr(reset));
  Register #(.width(32)) R6 (.D(delayer1x32_1_p2), .en(decoder_1_out6), .Q(R6_q), .clk(clk), .clr(reset));
  Register #(.width(32)) R7 (.D(delayer1x32_1_p2), .en(decoder_1_out7), .Q(R7_q), .clk(clk), .clr(reset));
  Register #(.width(32)) R8 (.D(delayer1x32_1_p2), .en(decoder_1_out8), .Q(R8_q), .clk(clk), .clr(reset));
  Register #(.width(32)) R9 (.D(delayer1x32_1_p2), .en(decoder_1_out9), .Q(R9_q), .clk(clk), .clr(reset));
  Register #(.width(32)) R10 (.D(delayer1x32_1_p2), .en(decoder_1_out10), .Q(R10_q), .clk(clk), .clr(reset));
  Register #(.width(32)) R11 (.D(delayer1x32_1_p2), .en(decoder_1_out11), .Q(R11_q), .clk(clk), .clr(reset));
  Register #(.width(32)) R12 (.D(delayer1x32_1_p2), .en(decoder_1_out12), .Q(R12_q), .clk(clk), .clr(reset));
  Register #(.width(32)) R13 (.D(delayer1x32_1_p2), .en(decoder_1_out13), .Q(R13_q), .clk(clk), .clr(reset));
  Register #(.width(32)) R14 (.D(delayer1x32_1_p2), .en(decoder_1_out14), .Q(R14_q), .clk(clk), .clr(reset));
  Register #(.width(32)) R15 (.D(delayer1x32_1_p2), .en(decoder_1_out15), .Q(R15_q), .clk(clk), .clr(reset));
  Register #(.width(32)) R16 (.D(delayer1x32_1_p2), .en(decoder_1_out16), .Q(R16_q), .clk(clk), .clr(reset));
  Register #(.width(32)) R17 (.D(delayer1x32_1_p2), .en(decoder_1_out17), .Q(R17_q), .clk(clk), .clr(reset));
  Register #(.width(32)) R18 (.D(delayer1x32_1_p2), .en(decoder_1_out18), .Q(R18_q), .clk(clk), .clr(reset));
  Register #(.width(32)) R19 (.D(delayer1x32_1_p2), .en(decoder_1_out19), .Q(R19_q), .clk(clk), .clr(reset));
  Register #(.width(32)) R20 (.D(delayer1x32_1_p2), .en(decoder_1_out20), .Q(R20_q), .clk(clk), .clr(reset));
  Register #(.width(32)) R21 (.D(delayer1x32_1_p2), .en(decoder_1_out21), .Q(R21_q), .clk(clk), .clr(reset));
  Register #(.width(32)) R22 (.D(delayer1x32_1_p2), .en(decoder_1_out22), .Q(R22_q), .clk(clk), .clr(reset));
  Register #(.width(32)) R23 (.D(delayer1x32_1_p2), .en(decoder_1_out23), .Q(R23_q), .clk(clk), .clr(reset));
  Register #(.width(32)) R24 (.D(delayer1x32_1_p2), .en(decoder_1_out24), .Q(R24_q), .clk(clk), .clr(reset));
  Register #(.width(32)) R25 (.D(delayer1x32_1_p2), .en(decoder_1_out25), .Q(R25_q), .clk(clk), .clr(reset));
  Register #(.width(32)) R26 (.D(delayer1x32_1_p2), .en(decoder_1_out26), .Q(R26_q), .clk(clk), .clr(reset));
  Register #(.width(32)) R27 (.D(delayer1x32_1_p2), .en(decoder_1_out27), .Q(R27_q), .clk(clk), .clr(reset));
  Register #(.width(32)) R28 (.D(delayer1x32_1_p2), .en(decoder_1_out28), .Q(R28_q), .clk(clk), .clr(reset));
  Register #(.width(32)) R29 (.D(delayer1x32_1_p2), .en(decoder_1_out29), .Q(R29_q), .clk(clk), .clr(reset));
  Register #(.width(32)) R30 (.D(delayer1x32_1_p2), .en(decoder_1_out30), .Q(R30_q), .clk(clk), .clr(reset));
  Register #(.width(32)) R31 (.D(delayer1x32_1_p2), .en(decoder_1_out31), .Q(R31_q), .clk(clk), .clr(reset));
  Multiplexer #(.select(5), .width(32), .enable("false")) multiplexer_1 (
    .in0({32{1'b0}}), .in1(R1_q), .in2(R2_q), .in3(R3_q), .in4(R4_q), .in5(R5_q), .in6(R6_q), .in7(R7_q),
    .in8(R8_q), .in9(R9_q), .in10(R10_q), .in11(R11_q), .in12(R12_q), .in13(R13_q), .in14(R14_q),
    .in15(R15_q), .in16(R16_q), .in17(R17_q), .in18(R18_q), .in19(R19_q), .in20(R20_q), .in21(R21_q),
    .in22(R22_q), .in23(R23_q), .in24(R24_q), .in25(R25_q), .in26(R26_q), .in27(R27_q), .in28(R28_q),
    .in29(R29_q), .in30(R30_q), .in31(R31_q), .out(multiplexer_1_out), .sel(Read_Register_1));
  Multiplexer #(.select(5), .width(32), .enable("false")) multiplexer_2 (
    .in0({32{1'b0}}), .in1(R1_q), .in2(R2_q), .in3(R3_q), .in4(R4_q), .in5(R5_q), .in6(R6_q), .in7(R7_q),
    .in8(R8_q), .in9(R9_q), .in10(R10_q), .in11(R11_q), .in12(R12_q), .in13(R13_q), .in14(R14_q),
    .in15(R15_q), .in16(R16_q), .in17(R17_q), .in18(R18_q), .in19(R19_q), .in20(R20_q), .in21(R21_q),
    .in22(R22_q), .in23(R23_q), .in24(R24_q), .in25(R25_q), .in26(R26_q), .in27(R27_q), .in28(R28_q),
    .in29(R29_q), .in30(R30_q), .in31(R31_q), .out(multiplexer_2_out), .sel(Read_Register_2));
  // Delayer1x32 delayer1x32_2: pin names not known; wires that end beside it: multiplexer_1_out, Read_Data_1
  // Delayer1x32 delayer1x32_3: pin names not known; wires that end beside it: multiplexer_2_out, Read_Data_2
endmodule

module ALU (
  input  [3:0] Operation,
  input  [31:0] A,
  input  [31:0] B,
  output Z,
  output [31:0] Result
);

  wire nor_1_out;
  wire [0:0] comparator_1_lt;
  wire [31:0] adder_1_out, and_1_out, multiplexer_1_out, multiplexer_2_out, multiplexer_3_out, not_1_out,
       not_2_out, or_1_out;

  assign not_1_out = ~A;  // NOT_Gate not_1, 32 bits wide
  assign not_2_out = ~B;  // NOT_Gate not_2, 32 bits wide
  Comparator #(.width(32)) comparator_1 (.a(A), .b(B), .lt(comparator_1_lt[0]));  // open: gt, eq
  Multiplexer #(.width(32), .enable("false")) multiplexer_1 (
    .in0(A), .in1(not_1_out), .out(multiplexer_1_out), .sel(Operation[3]));
  Multiplexer #(.width(32), .enable("false")) multiplexer_2 (
    .in0(B), .in1(not_2_out), .out(multiplexer_2_out), .sel(Operation[2]));
  assign and_1_out = multiplexer_1_out & multiplexer_2_out;  // AND_Gate and_1, 32 bits wide
  assign or_1_out = multiplexer_1_out | multiplexer_2_out;  // OR_Gate or_1, 32 bits wide
  Adder #(.width(32)) adder_1 (
    .a(multiplexer_1_out), .b(multiplexer_2_out), .out(adder_1_out), .cin(Operation[2]));  // open: cout
  Multiplexer #(.select(2), .width(32), .enable("false")) multiplexer_3 (
    .in0(and_1_out), .in1(or_1_out), .in2(adder_1_out), .in3({{31{1'b0}}, comparator_1_lt[0]}),
    .out(multiplexer_3_out), .sel(Operation[1:0]));
  nor nor_1 (nor_1_out, multiplexer_3_out[0], multiplexer_3_out[1], multiplexer_3_out[2], multiplexer_3_out[3], multiplexer_3_out[4], multiplexer_3_out[5], multiplexer_3_out[6], multiplexer_3_out[7], multiplexer_3_out[8], multiplexer_3_out[9], multiplexer_3_out[10], multiplexer_3_out[11], multiplexer_3_out[12], multiplexer_3_out[13], multiplexer_3_out[14], multiplexer_3_out[15], multiplexer_3_out[16], multiplexer_3_out[17], multiplexer_3_out[18], multiplexer_3_out[19], multiplexer_3_out[20], multiplexer_3_out[21], multiplexer_3_out[22], multiplexer_3_out[23], multiplexer_3_out[24], multiplexer_3_out[25], multiplexer_3_out[26], multiplexer_3_out[27], multiplexer_3_out[28], multiplexer_3_out[29], multiplexer_3_out[30], multiplexer_3_out[31]);
  // Delayer2x32 delayer2x32_1: pin names not known; wires that end beside it: multiplexer_3_out, Result
  // Delayer2x1 delayer2x1_1: pin names not known; wires that end beside it: nor_1_out, Z

  // Notes on the sheet:
  //   0001    OR
  //   Operation    Function
  //   0000    AND
  //   0010    add
  //   0110    subtract
  //   0111    set on less than
  //   1100    NOR
endmodule

module Data_Memory_32 (
  input  Write,
  input  [31:0] Address,
  input  [31:0] Write_Data,
  input  clk,
  input  reset,
  input  Read,
  output [31:0] Read_Data
);

  wire [9:0] bitselector_1_out;
  wire [31:0] delayer2x32_1_p2, ram_1_data;

  BitSelector #(.width(32), .group(10)) bitselector_1 (.in(Address), .out(bitselector_1_out), .sel(2'b00));
  // Delayer2x32 delayer2x32_1: pin names not known; wires that end beside it: Write_Data, delayer2x32_1_p2
  RAM #(.dataWidth(32), .bus("separate"), .Datafile_on_reset("TG00ram.txt")) ram_1 (
    .addr(bitselector_1_out[9:2]), .din(delayer2x32_1_p2), .data(ram_1_data), .str(Write), .sel(1'b1),
    .clk(clk), .ld(Read), .clr(reset));
  // Delayer2x32 delayer2x32_2: pin names not known; wires that end beside it: ram_1_data, Read_Data

  // Notes on the sheet:
  //   Memoria de 32 bits direccionable a nivel de byte
  //   Tan solo implementadas las 256 primeras posiciones de 32 bits o 1024 bytes
endmodule

module Instruction_memory (
  input  [31:0] Read_address,
  output [31:0] Instruction
);

  wire [6:0] bitselector_1_out;
  wire [31:0] ram_1_data;

  BitSelector #(.width(30), .group(7)) bitselector_1 (.in(Read_address[31:2]), .out(bitselector_1_out), .sel(3'b000));
  RAM #(.addrWidth(7), .dataWidth(32), .bus("asynch"), .Datafile_on_reset("TG00rom.txt")) ram_1 (
    .addr(bitselector_1_out), .data(ram_1_data), .sel(1'b1), .ld(1'b1), .clr(1'b0));
  // Delayer2x32 delayer2x32_1: pin names not known; wires that end beside it: ram_1_data, Instruction
endmodule

module Control_ALU (
  input  [2:0] OpALU,
  input  [5:0] funcion,
  output [3:0] OUT
);

  wire [3:0] multiplexer_1_out;

  Multiplexer #(.select(4), .width(4), .enable("false")) multiplexer_1 (
    .in0(4'b0010), .in2(4'b0110), .in4(4'b0000), .in5(4'b0001), .in10(4'b0111), .out(multiplexer_1_out),
    .sel(funcion[3:0]));  // open: in1, in3, in6, in7, in8, in9, in11, in12, in13, in14, in15
  Multiplexer #(.select(3), .width(4), .enable("false")) multiplexer_2 (
    .in0(4'b0010), .in1(4'b0110), .in2(4'b0000), .in3(4'b0001), .in4(4'b0111), .in5(4'b1100),
    .in7(multiplexer_1_out), .out(OUT), .sel(OpALU));  // open: in6

  // Notes on the sheet:
  //   OpALU    OUT
  //    000    add
  //    001    sub
  //    010    and
  //    011    or
  //   100    set on less than
  //   101    nor
  //   111    funcion (in)
endmodule

module ControladorDisp (
  input  [4:0] in_1,
  output [3:0] out_2,
  output [3:0] out_3
);

  wire [4:4] divider_1_out, divider_1_rem;

  Divider #(.width(5)) divider_1 (
    .a(in_1), .b(5'b01010), .out({divider_1_out[4], out_3}), .rem({divider_1_rem[4], out_2}));  // open: upper
endmodule

module funcion (
  input  [5:0] funcion,
  output ADD,
  output SUB,
  output AND,
  output OR,
  output SLT
);

  wire [5:5] multiplexer_1_out;

  Multiplexer #(.select(4), .width(6), .enable("false")) multiplexer_1 (
    .in0(6'b000001), .in2(6'b000010), .in4(6'b000100), .in5(6'b001000), .in10(6'b010000),
    .out({multiplexer_1_out[5], SLT, OR, AND, SUB, ADD}), .sel(funcion[3:0]));  // open: in1, in3, in6, in7, in8, in9, in11, in12, in13, in14, in15
endmodule

module OpALU (
  input  [5:0] in_1,
  output OUT
);

  and and_1 (OUT, ~in_1[0], ~in_1[1], ~in_1[2], ~in_1[3], ~in_1[4], ~in_1[5]);  // AND_Gate
endmodule
